# Fritzing sketch MQTT433gateway (saved by Fritzing 0.9.3b)
stripboards: 1

parts:
  ESP = HUZZAH ESP8266 Breakout
  U1 = Voltage Regulator - 5V [package="TO220 [THT]"]
  D1 = Rectifier Diode [part_number=1N4001 package="300 mil [THT]"]
  Power_plug1 = Power plug
  C4 = Tantalum Capacitor [capacitance=0.33µF voltage=20V package="100 mil [THT, tantalum]"]
  C5 = Tantalum Capacitor [capacitance=0.1µF package="100 mil [THT, tantalum]"]
  U2 = RF-LINK_RX [package=rf-link_rx]
  U3 = RF-LINK_TX [package=rf-link_tx]
  ANT1 = Antenna
  ANT2 = Antenna
  D2 = Rectifier Diode [part_number=1N4148 package="300 mil [THT]"]
  R1 = Resistor [tolerance=±5% resistance=1k package=THT]
  LED1 = LED - 5mm [color="Green (555nm)" package="5 mm [THT]"]

nets:
  5V: ESP.VIN, U1.output_voltage, C5.+, U2.+5V
  GND: ESP.GND, U1.GND, Power_plug1.GND, C4.-, C5.-, U2.GND, U3.GND
  N1: ESP.GPIO12, D2.anode
  3.3V: ESP.3.3V, LED1.anode
  N2: ESP.GPIO0, R1.Pin_0
  send: ESP.GPIO4, U3.DATA
  12V: U1.input_voltage, D1.cathode, C4.+, U3.+5V
  N3: D1.anode, Power_plug1.VCC
  recv: U2.DATA, D2.cathode
  N4: U2.ANT, ANT1.antenna_lead
  N5: U3.ANT, ANT2.antenna_lead
  N6: R1.Pin_1, LED1.cathode

custom parts:
  HUZZAH ESP8266 Breakout: The ESP8266 processor from Espressif is an 80 MHz microcontroller with a full WiFi front-end (both as client and access point) and TCP/IP stack with DNS support as well.
